// Logisim project regfile-harness.circ as structural Verilog: 1 circuit, main circuit main
module main (
  output [31:0] out_1,
  output [31:0] out_2,
  output [31:0] out_3,
  output [31:0] out_4,
  output [31:0] out_5,
  output [31:0] out_6,
  output [31:0] out_7,
  output [31:0] out_8,
  output [31:0] out_9,
  output halt
);

  wire clk, we;
  wire [4:0] rd, rs1, rs2;
  wire [7:0] adder_1_out, In;
  wire [31:0] w;

  Register register_1 (.D(adder_1_out), .Q(In), .clk(clk));  // open: en, clr
  Clock clock_1 (.out(clk));
  Comparator #(.mode("unsigned")) comparator_1 (.a({8{1'b1}}), .b(In), .eq(halt));  // open: gt, lt
  Adder adder_1 (.a(8'h1), .b(In), .out(adder_1_out));  // open: cin, cout
  ROM #(.dataWidth(1)) rom_1 (.addr(In), .data(we), .sel(1'b1));
  ROM #(.dataWidth(5)) rom_2 (.addr(In), .data(rd), .sel(1'b1));
  ROM #(.dataWidth(5)) rom_3 (.addr(In), .data(rs1), .sel(1'b1));
  ROM #(.dataWidth(5)) rom_4 (.addr(In), .data(rs2), .sel(1'b1));
  ROM #(.dataWidth(32)) rom_5 (.addr(In), .data(w), .sel(1'b1));
  RegFile regfile_1 (
    .Clk(clk), .R1(out_1), .R2(out_2), .WE(we), .W(w), .RD(rd), .RS1(rs1), .RS2(rs2), .s0(out_3), .s1(out_4),
    .t0(out_5), .t1(out_6), .a0(out_7), .ra(out_8), .sp(out_9));

  // Other names for the same wires on the sheet: a0[31:0] = out_7; r1[31:0] = out_1; r2[31:0] = out_2;
  //   ra[31:0] = out_8; s0[31:0] = out_3; s1[31:0] = out_4; sp[31:0] = out_9; t0[31:0] = out_5; t1[31:0] = out_6

  // Notes on the sheet:
  //   Counter
  //   Halt signal
  //   There should be no red/blue wires and the outputs should not be x's
endmodule
