// Logisim project regfile.circ as structural Verilog: 5 circuits, main circuit RegFile
module RegFile (
  input  [4:0] RD,
  input  [4:0] RS1,
  input  [4:0] RS2,
  input  [31:0] W,
  input  WE,
  input  Clk,
  output [31:0] s0,
  output [31:0] s1,
  output [31:0] t0,
  output [31:0] t1,
  output [31:0] a0,
  output [31:0] ra,
  output [31:0] sp,
  output [31:0] R1,
  output [31:0] R2
);

  wire A0_t, A1, RA_t, S0_t, S1_t, SP_t, T0_t, T1_t;
  wire [31:0] a1_t;

  Demultiplexer #(.select(5)) demultiplexer_1 (
    .out1(RA_t), .out2(SP_t), .out5(T0_t), .out6(T1_t), .out8(S0_t), .out9(S1_t), .out10(A0_t), .out11(A1),
    .in(WE), .sel(RD));  // open: out0, out3, out4, out7, out12, out13, out14, out15, out16, out17, out18, out19, out20, out21, out22, out23, out24, out25, out26, out27, out28, out29, out30, out31, en
  Register #(.width(32)) register_1 (.D(W), .en(RA_t), .Q(ra), .clk(Clk));  // open: clr
  Register #(.width(32)) register_2 (.D(W), .en(SP_t), .Q(sp), .clk(Clk));  // open: clr
  Register #(.width(32)) register_3 (.D(W), .en(T0_t), .Q(t0), .clk(Clk));  // open: clr
  Register #(.width(32)) register_4 (.D(W), .en(T1_t), .Q(t1), .clk(Clk));  // open: clr
  Register #(.width(32)) register_5 (.D(W), .en(S0_t), .Q(s0), .clk(Clk));  // open: clr
  Register #(.width(32)) register_6 (.D(W), .en(S1_t), .Q(s1), .clk(Clk));  // open: clr
  Register #(.width(32)) register_7 (.D(W), .en(A0_t), .Q(a0), .clk(Clk));  // open: clr
  Register #(.width(32)) register_8 (.D(W), .en(A1), .Q(a1_t), .clk(Clk));  // open: clr
  Read_Data1 Read_data1 (
    .RA(ra), .SP(sp), .T0(t0), .T1(t1), .S0(s0), .S1(s1), .A0(a0), .A1(a1_t), .Read_data1(R1), .RS1(RS1));  // open: T2
  Read_data2 Read_data2 (
    .RA(ra), .SP(sp), .T0(t0), .T1(t1), .S0(s0), .S1(s1), .A0(a0), .A1(a1_t), .Read_data2(R2), .RS2(RS2));  // open: T2

  // Notes on the sheet:
  //   Write Register
  //   Read Register 1
  //   Read Register 2
  //   Write Data
  //   Write Enable
  //   Clock
  //   NOTE
  //   Please do not modify/replace/move/change/delete/etc input and output pins
  //   These are debug/test outputs from your circuit
  //   Read Data 1
  //   Read Data 2
endmodule

module DMX (
  input  Write_enable,
  input  [4:0] write_register,
  output RA,
  output SP,
  output T0,
  output T1,
  output S0,
  output S1,
  output A0
);

  Demultiplexer #(.select(5)) demultiplexer_1 (
    .out1(RA), .out2(SP), .out5(T0), .out6(T1), .out8(S0), .out9(S1), .out10(A0), .in(Write_enable),
    .sel(write_register));  // open: out0, out3, out4, out7, out11, out12, out13, out14, out15, out16, out17, out18, out19, out20, out21, out22, out23, out24, out25, out26, out27, out28, out29, out30, out31, en
endmodule

module Write_data (
  input  [31:0] Write_data,
  input  write_enable,
  input  [4:0] Write_register,
  output [31:0] x1,
  output [31:0] x0,
  output [31:0] x2,
  output [31:0] x5,
  output [31:0] x6,
  output [31:0] x8,
  output [31:0] x9,
  output [31:0] x10,
  output [31:0] x11
);

  Demultiplexer #(.select(5), .width(32)) demultiplexer_1 (
    .out0(x0), .out1(x1), .out2(x2), .out5(x5), .out6(x6), .out8(x8), .out9(x9), .out10(x10), .out11(x11),
    .in(Write_data), .sel(Write_register), .en(write_enable));  // open: out3, out4, out7, out12, out13, out14, out15, out16, out17, out18, out19, out20, out21, out22, out23, out24, out25, out26, out27, out28, out29, out30, out31
endmodule

module Read_Data1 (
  input  [31:0] RA,
  input  [31:0] SP,
  input  [31:0] T0,
  input  [31:0] T1,
  input  [31:0] T2,
  input  [4:0] RS1,
  input  [31:0] S0,
  input  [31:0] S1,
  input  [31:0] A0,
  input  [31:0] A1,
  output [31:0] Read_data1
);

  Multiplexer #(.select(5), .width(32)) multiplexer_1 (
    .in0({32{1'b0}}), .in1(RA), .in2(SP), .in5(T0), .in6(T1), .in7(T2), .in8(S0), .in9(S1), .in10(A0),
    .in11(A1), .out(Read_data1), .sel(RS1));  // open: in3, in4, in12, in13, in14, in15, in16, in17, in18, in19, in20, in21, in22, in23, in24, in25, in26, in27, in28, in29, in30, in31, en
endmodule

module Read_data2 (
  input  [31:0] RA,
  input  [31:0] SP,
  input  [31:0] T0,
  input  [31:0] T1,
  input  [31:0] T2,
  input  [4:0] RS2,
  input  [31:0] S0,
  input  [31:0] S1,
  input  [31:0] A0,
  input  [31:0] A1,
  output [31:0] Read_data2
);

  Multiplexer #(.select(5), .width(32)) multiplexer_1 (
    .in0({32{1'b0}}), .in1(RA), .in2(SP), .in5(T0), .in6(T1), .in7(T2), .in8(S0), .in9(S1), .in10(A0),
    .in11(A1), .out(Read_data2), .sel(RS2));  // open: in3, in4, in12, in13, in14, in15, in16, in17, in18, in19, in20, in21, in22, in23, in24, in25, in26, in27, in28, in29, in30, in31, en
endmodule
